// Logisim project ALU.circ as structural Verilog: 1 circuit, main circuit main
module main (
  input  [31:0] dataA,
  input  [31:0] dataB,
  input  [3:0] OpSelector,
  output [31:0] dataOut
);

  wire comparator_1_lt, comparator_2_lt;
  wire [31:0] add_out, and_out, or_out, sll_out, slt_out, slt_uns_out, srl_out, sub_out, xor_out;

  Multiplexer #(.select(4), .width(32), .enable("false")) multiplexer_1 (
    .in0(add_out), .in1(sll_out), .in2(slt_out), .in3(slt_uns_out), .in4(xor_out), .in5(srl_out),
    .in6(or_out), .in7(and_out), .in8(sub_out), .in9(srl_out), .out(dataOut), .sel(OpSelector));  // open: in10, in11, in12, in13, in14, in15
  Adder #(.width(32)) adder_1 (.a(dataA), .b(dataA), .out(add_out));  // open: cin, cout
  Shifter #(.width(32), .shift("lr")) shifter_1 (.in(dataA), .\dist (dataA[4:0]), .out(srl_out));
  Shifter #(.width(32)) shifter_2 (.in(dataA), .\dist (dataA[4:0]), .out(sll_out));
  assign or_out = dataA | dataA;  // OR_Gate or_1, 32 bits wide
  assign and_out = dataA & dataA;  // AND_Gate and_1, 32 bits wide
  Comparator #(.width(32)) comparator_1 (.a(dataA), .b(dataA), .lt(comparator_1_lt));  // open: gt, eq
  assign slt_out = {{31{1'b0}}, comparator_1_lt};  // Bit_Extender bit_extender_1
  Comparator #(.width(32), .mode("unsigned")) comparator_2 (
    .a(dataA), .b(dataA), .lt(comparator_2_lt));  // open: gt, eq
  Subtractor #(.width(32)) subtractor_1 (.a(dataA), .b(dataA), .out(sub_out));  // open: bin, bout
  assign slt_uns_out = {{31{1'b0}}, comparator_2_lt};  // Bit_Extender bit_extender_2
  assign xor_out = dataA ^ dataA;  // XOR_Gate xor_1, 32 bits wide
  Shifter #(.width(32), .shift("ar")) shifter_3 (.in(dataA), .\dist (dataA[4:0]), .out(srl_out));

  assign dataB = dataA;

  // Notes on the sheet:
  //   choose the result to be returned.
  //   adder 0000
  //   shift right logical 0101
  //   shift left logical 0001
  //   logical or 0110
  //   set less than 0010
  //   logical and 0111
  //   subtractor 1000
  //   set less than unsigned 0011
  //   exclusive or (xor) 0100
  //   shift right arithmetic and 1101
endmodule
