// Logisim project ProgramCounter.circ as structural Verilog: 1 circuit, main circuit main
module main (
  input  [31:0] InPC,
  input  clk,
  output [31:0] OutPC_4,
  output [31:0] OutPCJumps
);

  Register #(.width(32), .Select("low")) register_1 (.D(InPC), .en(1'b1), .Q(OutPCJumps), .clk(clk));  // open: clr
  Adder #(.width(32)) adder_1 (.a(OutPCJumps), .b(32'h4), .out(OutPC_4));  // open: cin, cout
endmodule
