// Logisim project RV32IDatapath.circ as structural Verilog: 10 circuits, main circuit main
module main (
);

  wire ALUSrc_arithm, ALUSrc_mem, branch, clock_1_out, controlunit_1_alusrc_arithm, controlunit_1_alusrc_mem,
       controlunit_1_memread, controlunit_1_memwrite, controlunit_1_regwritealu, controlunit_1_regwritemem,
       inst1Mem, mem_read, mem_write, register_3_q, register_4_q, register_5_q, register_6_q, register_15_q,
       register_16_q, regwrite_ALU, regwrite_mem;
  wire [2:0] funct3_p1, funct3_p2;
  wire [3:0] ALUOp_arithm, ALUOp_mem, controlunit_1_aluop_arithm, controlunit_1_aluop_mem;
  wire [4:0] rd_p1, rd_p2, rs1_p1, rs1_p2, rs2_p1, rs2_p2;
  wire [6:0] funct7_p1, funct7_p2, opcode_p1, opcode_p2;
  wire [23:0] bit_extender_1_out, bit_extender_2_out;
  wire [31:0] adder_1_out, alu_1_aluout, alu_2_aluout, ALUvalue, branchpredictionunit_1_destaddr, EXMEM_q,
       IFID_q, imm, imm_p1, imm_p2, inst1, inst2, memvalue, multiplexer_1_out, multiplexer_4_out,
       multiplexer_5_out, multiplexer_6_out, multiplexer_7_out, PC_q, ram_1_dout, register_1_q, register_2_q,
       register_11_q, register_12_q, register_13_q, register_14_q, register_19_q, registers_1_rs1_out_p1,
       registers_1_rs1_out_p2, registers_1_rs2_out_p1, registers_1_rs2_out_p2, rs1V, rs2V;

  Clock clock_1 (.out(clock_1_out));
  Multiplexer #(.width(32)) multiplexer_1 (
    .in0(adder_1_out), .in1(branchpredictionunit_1_destaddr), .out(multiplexer_1_out), .sel(branch));
  Register #(.width(32)) PC (.D(multiplexer_1_out), .en(1'b1), .clk(clock_1_out), .Q(PC_q));  // open: clr
  Adder #(.width(32)) adder_1 (.a(32'h4), .b(PC_q), .out(adder_1_out));  // open: cin, cout
  ROM #(.addrWidth(24), .dataWidth(64)) ArithmeticInstructionsMem (.addr(bit_extender_1_out), .data({inst2, inst1}));
  Bit_Extender #(.in_width(32), .out_width(24)) bit_extender_1 (.in(PC_q), .out(bit_extender_1_out));
  Register #(.width(32)) IFID (.D(PC_q), .en(1'b1), .Q(IFID_q));  // open: clk, clr
  Register #(.width(32)) register_1 (.D(inst1), .en(1'b1), .clk(clock_1_out), .Q(register_1_q));  // open: clr
  Register #(.width(32)) register_2 (.D(inst2), .en(1'b1), .clk(clock_1_out), .Q(register_2_q));  // open: clr
  ControlUnit controlunit_1 (
    .instruction2Type(register_2_q), .instruction1Type(register_1_q),
    .regWriteALU(controlunit_1_regwritealu), .regWriteMem(controlunit_1_regwritemem),
    .memWrite(controlunit_1_memwrite), .memRead(controlunit_1_memread),
    .ALUSrc_arithm(controlunit_1_alusrc_arithm), .ALUSrc_mem(controlunit_1_alusrc_mem),
    .ALUOp_arithm(controlunit_1_aluop_arithm), .ALUOp_mem(controlunit_1_aluop_mem), .branch(branch),
    .inst1Mem(inst1Mem));
  Registers registers_1 (
    .r_data_p2(memvalue), .r_data_p1(ALUvalue), .WE_p1(regwrite_ALU), .rs1_addr_p1(rs1_p1),
    .rs1_addr_p2(rs1_p2), .rd_addr_p1(rd_p1), .WE_p2(regwrite_mem), .rs2_addr_p1(rs2_p1),
    .rs2_addr_p2(rs2_p2), .rd_addr_p2(rd_p2), .rs1_out_p1(registers_1_rs1_out_p1),
    .rs1_out_p2(registers_1_rs1_out_p2), .rs2_out_p1(registers_1_rs2_out_p1),
    .rs2_out_p2(registers_1_rs2_out_p2));
  InstructionDecoder instructiondecoder_1 (
    .Instruction(register_1_q), .Imm(imm_p1), .rd(rd_p1), .rs1(rs1_p1), .rs2(rs2_p1), .funct3(funct3_p1),
    .funct7(funct7_p1), .opcode(opcode_p1));
  InstructionDecoder instructiondecoder_2 (
    .Instruction(register_2_q), .Imm(imm_p2), .rd(rd_p2), .rs1(rs1_p2), .rs2(rs2_p2), .funct3(funct3_p2),
    .funct7(funct7_p2), .opcode(opcode_p2));
  BranchPredictionUnit branchpredictionunit_1 (
    .currentPC(IFID_q), .imm(rs1V), .rs2(rs2V), .rs1(imm), .branch(branch), .clk(clock_1_out),
    .funct3(funct3_p1), .destAddr(branchpredictionunit_1_destaddr));
  Multiplexer #(.width(32)) multiplexer_2 (
    .in0(registers_1_rs1_out_p1), .in1(registers_1_rs1_out_p2), .out(rs1V), .sel(inst1Mem));
  Multiplexer #(.width(32)) multiplexer_3 (
    .in0(registers_1_rs2_out_p1), .in1(registers_1_rs2_out_p2), .out(rs2V), .sel(inst1Mem));
  Multiplexer #(.width(32)) multiplexer_4 (
    .in0(registers_1_rs1_out_p2), .in1(registers_1_rs1_out_p1), .out(multiplexer_4_out), .sel(inst1Mem));
  Multiplexer #(.width(32)) multiplexer_5 (
    .in0(registers_1_rs2_out_p2), .in1(registers_1_rs2_out_p1), .out(multiplexer_5_out), .sel(inst1Mem));
  Register #(.width(1)) register_3 (
    .D(controlunit_1_regwritealu), .en(1'b1), .clk(clock_1_out), .Q(register_3_q));  // open: clr
  Register #(.width(1)) register_4 (
    .D(controlunit_1_regwritemem), .en(1'b1), .clk(clock_1_out), .Q(register_4_q));  // open: clr
  Register #(.width(1)) register_5 (
    .D(controlunit_1_memwrite), .en(1'b1), .clk(clock_1_out), .Q(register_5_q));  // open: clr
  Register #(.width(1)) register_6 (
    .D(controlunit_1_memread), .en(1'b1), .clk(clock_1_out), .Q(register_6_q));  // open: clr
  Register #(.width(1)) register_7 (
    .D(controlunit_1_alusrc_arithm), .en(1'b1), .clk(clock_1_out), .Q(ALUSrc_arithm));  // open: clr
  Register #(.width(1)) register_8 (
    .D(controlunit_1_alusrc_mem), .en(1'b1), .clk(clock_1_out), .Q(ALUSrc_mem));  // open: clr
  Register #(.width(4)) register_9 (
    .D(controlunit_1_aluop_arithm), .en(1'b1), .clk(clock_1_out), .Q(ALUOp_arithm));  // open: clr
  Register #(.width(4)) register_10 (
    .D(controlunit_1_aluop_mem), .en(1'b1), .clk(clock_1_out), .Q(ALUOp_mem));  // open: clr
  Register #(.width(32)) IDEX (.D(branchpredictionunit_1_destaddr), .en(1'b1), .clk(clock_1_out));  // open: Q, clr
  Register #(.width(32)) register_11 (.D(rs1V), .en(1'b1), .clk(clock_1_out), .Q(register_11_q));  // open: clr
  Register #(.width(32)) register_12 (.D(rs2V), .en(1'b1), .clk(clock_1_out), .Q(register_12_q));  // open: clr
  Register #(.width(32)) register_13 (
    .D(multiplexer_4_out), .en(1'b1), .clk(clock_1_out), .Q(register_13_q));  // open: clr
  Register #(.width(32)) register_14 (
    .D(multiplexer_5_out), .en(1'b1), .clk(clock_1_out), .Q(register_14_q));  // open: clr
  Multiplexer #(.width(32)) multiplexer_6 (
    .in0(register_12_q), .in1(imm), .out(multiplexer_6_out), .sel(ALUSrc_arithm));
  Multiplexer #(.width(32)) multiplexer_7 (.in0(register_14_q), .in1(imm), .out(multiplexer_7_out), .sel(ALUSrc_mem));
  Register #(.width(1)) register_15 (.D(register_3_q), .en(1'b1), .clk(clock_1_out), .Q(register_15_q));  // open: clr
  Register #(.width(1)) register_16 (.D(register_4_q), .en(1'b1), .clk(clock_1_out), .Q(register_16_q));  // open: clr
  Register #(.width(1)) register_17 (.D(register_5_q), .en(1'b1), .clk(clock_1_out), .Q(mem_write));  // open: clr
  Register #(.width(1)) register_18 (.D(register_6_q), .en(1'b1), .clk(clock_1_out), .Q(mem_read));  // open: clr
  Register #(.width(32)) EXMEM (.D(alu_1_aluout), .en(1'b1), .clk(clock_1_out), .Q(EXMEM_q));  // open: clr
  ALU alu_1 (.DataA(register_11_q), .DataB(multiplexer_6_out), .ALU_op(ALUOp_arithm), .ALUOut(alu_1_aluout));
  Register #(.width(32)) register_19 (.D(alu_2_aluout), .en(1'b1), .clk(clock_1_out), .Q(register_19_q));  // open: clr
  ALU alu_2 (.DataA(register_13_q), .DataB(multiplexer_7_out), .ALU_op(ALUOp_mem), .ALUOut(alu_2_aluout));
  RAM #(.addrWidth(24), .dataWidth(32)) ram_1 (
    .addr(bit_extender_2_out), .we(mem_write), .oe(mem_read), .clk(clock_1_out), .din(rs2V), .dout(ram_1_dout));
  Bit_Extender #(.in_width(32), .out_width(24)) bit_extender_2 (.in(register_19_q), .out(bit_extender_2_out));
  Register #(.width(1)) register_20 (.D(register_15_q), .en(1'b1), .clk(clock_1_out), .Q(regwrite_ALU));  // open: clr
  Register #(.width(1)) register_21 (.D(register_16_q), .en(1'b1), .clk(clock_1_out), .Q(regwrite_mem));  // open: clr
  Register #(.width(32)) MEMWB (.D(EXMEM_q), .en(1'b1), .clk(clock_1_out), .Q(ALUvalue));  // open: clr
  Register #(.width(32)) register_22 (.D(ram_1_dout), .en(1'b1), .clk(clock_1_out), .Q(memvalue));  // open: clr

  // Notes on the sheet:
  //   IF STAGE
  //   access the instruction mem. and collect instructions
  //   calculate the branch address to the instruction
  //   ID STAGE
  //   select the registers used on the pipelines
  //   select the type and split each instruction
  //   EX STAGE
  //   Arithmetic instructions ALU
  //   Mem access instructions ALU
  //   MEM STAGE
  //   WB STAGE
endmodule

module Registers (
  input  [31:0] r_data_p2,
  input  [31:0] r_data_p1,
  input  WE_p1,
  input  [4:0] rs1_addr_p1,
  input  [4:0] rs1_addr_p2,
  input  [4:0] rd_addr_p1,
  input  WE_p2,
  input  [4:0] rs2_addr_p1,
  input  [4:0] rs2_addr_p2,
  input  [4:0] rd_addr_p2,
  output [31:0] rs1_out_p1,
  output [31:0] rs1_out_p2,
  output [31:0] rs2_out_p1,
  output [31:0] rs2_out_p2
);

  wire and_1_out, clock_1_out, WEx1, WEx2, WEx3, WEx4, WEx5, WEx6, WEx7, WEx8, WEx9, WEx10, WEx11, WEx12,
       WEx13, WEx14, WEx15, WEx16, WEx17, WEx18, WEx19, WEx20, WEx21, WEx22, WEx23, WEx24, WEx25, WEx26,
       WEx27, WEx28, WEx29, WEx30, WEx31;
  wire [31:0] multiplexer_1_out, OUTx1, OUTx2, OUTx3, OUTx4, OUTx5, OUTx6, OUTx7, OUTx8, OUTx9, OUTx10,
       OUTx11, OUTx12, OUTx13, OUTx14, OUTx15, OUTx16, OUTx17, OUTx18, OUTx19, OUTx20, OUTx21, OUTx22,
       OUTx23, OUTx24, OUTx25, OUTx26, OUTx27, OUTx28, OUTx29, OUTx30, OUTx31;

  Demultiplexer #(.select(5)) demultiplexer_1 (
    .out1(WEx1), .out2(WEx2), .out3(WEx3), .out4(WEx4), .out5(WEx5), .out6(WEx6), .out7(WEx7), .out8(WEx8),
    .out9(WEx9), .out10(WEx10), .out11(WEx11), .out12(WEx12), .out13(WEx13), .out14(WEx14), .out15(WEx15),
    .out16(WEx16), .out17(WEx17), .out18(WEx18), .out19(WEx19), .out20(WEx20), .out21(WEx21), .out22(WEx22),
    .out23(WEx23), .out24(WEx24), .out25(WEx25), .out26(WEx26), .out27(WEx27), .out28(WEx28), .out29(WEx29),
    .out30(WEx30), .out31(WEx31), .in(WE_p1), .sel(rd_addr_p1));  // open: out0
  Demultiplexer #(.select(5)) demultiplexer_2 (
    .out1(WEx1), .out2(WEx2), .out3(WEx3), .out4(WEx4), .out5(WEx5), .out6(WEx6), .out7(WEx7), .out8(WEx8),
    .out10(WEx10), .out11(WEx11), .out12(WEx12), .out13(WEx13), .out14(WEx14), .out15(WEx15), .out16(WEx16),
    .out17(WEx17), .out18(WEx18), .out19(WEx19), .out20(WEx20), .out21(WEx21), .out22(WEx22), .out24(WEx24),
    .out25(WEx25), .out26(WEx26), .out27(WEx27), .out28(WEx28), .out29(WEx29), .out30(WEx30), .out31(WEx31),
    .in(WE_p2), .sel(rd_addr_p2));  // open: out0, out9, out23
  and and_1 (and_1_out, WE_p1, 1'b1);
  Multiplexer #(.width(32)) multiplexer_1 (.in0(r_data_p2), .in1(r_data_p1), .out(multiplexer_1_out), .sel(and_1_out));
  Clock clock_1 (.out(clock_1_out));
  Register #(.width(32)) x4 (.D(multiplexer_1_out), .en(WEx4), .clk(clock_1_out), .Q(OUTx4));  // open: clr
  Register #(.width(32)) x8 (.D(multiplexer_1_out), .en(WEx8), .clk(clock_1_out), .Q(OUTx8));  // open: clr
  Register #(.width(32)) x12 (.D(multiplexer_1_out), .en(WEx12), .clk(clock_1_out), .Q(OUTx12));  // open: clr
  Register #(.width(32)) x16 (.D(multiplexer_1_out), .en(WEx16), .clk(clock_1_out), .Q(OUTx16));  // open: clr
  Register #(.width(32)) x20 (.D(multiplexer_1_out), .en(WEx20), .clk(clock_1_out), .Q(OUTx20));  // open: clr
  Register #(.width(32)) x24 (.D(multiplexer_1_out), .en(WEx24), .clk(clock_1_out), .Q(OUTx24));  // open: clr
  Register #(.width(32)) x28 (.D(multiplexer_1_out), .en(WEx28), .clk(clock_1_out), .Q(OUTx28));  // open: clr
  Register #(.width(32)) x1 (.D(multiplexer_1_out), .en(WEx1), .clk(clock_1_out), .Q(OUTx1));  // open: clr
  Register #(.width(32)) x5 (.D(multiplexer_1_out), .en(WEx5), .clk(clock_1_out), .Q(OUTx5));  // open: clr
  Register #(.width(32)) x9 (.D(multiplexer_1_out), .en(WEx9), .clk(clock_1_out), .Q(OUTx9));  // open: clr
  Register #(.width(32)) x13 (.D(multiplexer_1_out), .en(WEx13), .clk(clock_1_out), .Q(OUTx13));  // open: clr
  Register #(.width(32)) x17 (.D(multiplexer_1_out), .en(WEx17), .clk(clock_1_out), .Q(OUTx17));  // open: clr
  Register #(.width(32)) x21 (.D(multiplexer_1_out), .en(WEx21), .clk(clock_1_out), .Q(OUTx21));  // open: clr
  Register #(.width(32)) x25 (.D(multiplexer_1_out), .en(WEx25), .clk(clock_1_out), .Q(OUTx25));  // open: clr
  Register #(.width(32)) x29 (.D(multiplexer_1_out), .en(WEx29), .clk(clock_1_out), .Q(OUTx29));  // open: clr
  Register #(.width(32)) x2 (.D(multiplexer_1_out), .en(WEx2), .clk(clock_1_out), .Q(OUTx2));  // open: clr
  Register #(.width(32)) x6 (.en(WEx6), .clk(clock_1_out), .Q(OUTx6));  // open: D, clr
  Register #(.width(32)) x10 (.D(multiplexer_1_out), .en(WEx10), .clk(clock_1_out), .Q(OUTx10));  // open: clr
  Register #(.width(32)) x14 (.D(multiplexer_1_out), .en(WEx14), .clk(clock_1_out), .Q(OUTx14));  // open: clr
  Register #(.width(32)) x18 (.D(multiplexer_1_out), .en(WEx18), .clk(clock_1_out), .Q(OUTx18));  // open: clr
  Register #(.width(32)) x22 (.D(multiplexer_1_out), .en(WEx22), .clk(clock_1_out), .Q(OUTx22));  // open: clr
  Register #(.width(32)) x26 (.D(multiplexer_1_out), .en(WEx26), .clk(clock_1_out), .Q(OUTx26));  // open: clr
  Register #(.width(32)) x30 (.D(multiplexer_1_out), .en(WEx30), .clk(clock_1_out), .Q(OUTx30));  // open: clr
  Register #(.width(32)) x3 (.D(multiplexer_1_out), .en(WEx3), .clk(clock_1_out), .Q(OUTx3));  // open: clr
  Register #(.width(32)) x7 (.D(multiplexer_1_out), .en(WEx7), .clk(clock_1_out), .Q(OUTx7));  // open: clr
  Register #(.width(32)) x11 (.D(multiplexer_1_out), .en(WEx11), .clk(clock_1_out), .Q(OUTx11));  // open: clr
  Register #(.width(32)) x15 (.D(multiplexer_1_out), .en(WEx15), .clk(clock_1_out), .Q(OUTx15));  // open: clr
  Register #(.width(32)) x19 (.D(multiplexer_1_out), .en(WEx19), .clk(clock_1_out), .Q(OUTx19));  // open: clr
  Register #(.width(32)) x23 (.D(multiplexer_1_out), .en(WEx23), .clk(clock_1_out), .Q(OUTx23));  // open: clr
  Register #(.width(32)) x27 (.D(multiplexer_1_out), .en(WEx27), .clk(clock_1_out), .Q(OUTx27));  // open: clr
  Register #(.width(32)) x31 (.D(multiplexer_1_out), .en(WEx31), .clk(clock_1_out), .Q(OUTx31));  // open: clr
  Multiplexer #(.select(5), .width(32)) multiplexer_2 (
    .in1(OUTx1), .in2(OUTx2), .in3(OUTx3), .in4(OUTx4), .in5(OUTx5), .in6(OUTx6), .in7(OUTx7), .in8(OUTx8),
    .in9(OUTx9), .in10(OUTx10), .in11(OUTx11), .in12(OUTx12), .in13(OUTx13), .in14(OUTx14), .in15(OUTx15),
    .in16(OUTx16), .in17(OUTx17), .in18(OUTx18), .in19(OUTx19), .in20(OUTx20), .in21(OUTx21), .in22(OUTx22),
    .in23(OUTx23), .in24(OUTx24), .in25(OUTx25), .in26(OUTx26), .in27(OUTx27), .in28(OUTx28), .in29(OUTx29),
    .in30(OUTx30), .in31(OUTx31), .out(rs1_out_p1), .sel(rs1_addr_p1));  // open: in0
  Multiplexer #(.select(5), .width(32)) multiplexer_3 (
    .in1(OUTx1), .in2(OUTx2), .in3(OUTx3), .in4(OUTx4), .in5(OUTx5), .in6(OUTx6), .in7(OUTx7), .in8(OUTx8),
    .in9(OUTx9), .in10(OUTx10), .in11(OUTx11), .in12(OUTx12), .in13(OUTx13), .in14(OUTx14), .in15(OUTx15),
    .in16(OUTx16), .in17(OUTx17), .in18(OUTx18), .in19(OUTx19), .in20(OUTx20), .in21(OUTx21), .in22(OUTx22),
    .in23(OUTx23), .in24(OUTx24), .in25(OUTx25), .in26(OUTx26), .in27(OUTx27), .in28(OUTx28), .in29(OUTx29),
    .in30(OUTx30), .in31(OUTx31), .out(rs2_out_p1), .sel(rs2_addr_p1));  // open: in0
  Multiplexer #(.select(5), .width(32)) multiplexer_4 (
    .in1(OUTx1), .in2(OUTx2), .in3(OUTx3), .in4(OUTx4), .in5(OUTx5), .in6(OUTx6), .in7(OUTx7), .in8(OUTx8),
    .in9(OUTx9), .in10(OUTx10), .in11(OUTx11), .in12(OUTx12), .in13(OUTx13), .in14(OUTx14), .in15(OUTx15),
    .in16(OUTx16), .in17(OUTx17), .in18(OUTx18), .in19(OUTx19), .in20(OUTx20), .in21(OUTx21), .in22(OUTx22),
    .in23(OUTx23), .in24(OUTx24), .in25(OUTx25), .in26(OUTx26), .in27(OUTx27), .in28(OUTx28), .in29(OUTx29),
    .in30(OUTx30), .in31(OUTx31), .out(rs1_out_p2), .sel(rs1_addr_p2));  // open: in0
  Multiplexer #(.select(5), .width(32)) multiplexer_5 (
    .in1(OUTx1), .in2(OUTx2), .in3(OUTx3), .in4(OUTx4), .in5(OUTx5), .in6(OUTx6), .in7(OUTx7), .in8(OUTx8),
    .in9(OUTx9), .in10(OUTx10), .in11(OUTx11), .in12(OUTx12), .in13(OUTx13), .in14(OUTx14), .in15(OUTx15),
    .in16(OUTx16), .in17(OUTx17), .in18(OUTx18), .in19(OUTx19), .in20(OUTx20), .in21(OUTx21), .in22(OUTx22),
    .in23(OUTx23), .in24(OUTx24), .in25(OUTx25), .in26(OUTx26), .in27(OUTx27), .in28(OUTx28), .in29(OUTx29),
    .in30(OUTx30), .in31(OUTx31), .out(rs2_out_p2), .sel(rs2_addr_p2));  // open: in0
  // also tied to GND on the sheet: {multiplexer_1_out[0], multiplexer_1_out[1], multiplexer_1_out[2], multiplexer_1_out[3], multiplexer_1_out[4], multiplexer_1_out[5], multiplexer_1_out[6], multiplexer_1_out[7], multiplexer_1_out[8], multiplexer_1_out[9], multiplexer_1_out[10], multiplexer_1_out[11], multiplexer_1_out[12], multiplexer_1_out[13], multiplexer_1_out[14], multiplexer_1_out[15], multiplexer_1_out[16], multiplexer_1_out[17], multiplexer_1_out[18], multiplexer_1_out[19], multiplexer_1_out[20], multiplexer_1_out[21], multiplexer_1_out[22], multiplexer_1_out[23], multiplexer_1_out[24], multiplexer_1_out[25], multiplexer_1_out[26], multiplexer_1_out[27], multiplexer_1_out[28], multiplexer_1_out[29], multiplexer_1_out[30], multiplexer_1_out[31]}

  // Notes on the sheet:
  //   select the data to be written (priority p1)
endmodule

module ALU (
  input  [31:0] DataA,
  input  [31:0] DataB,
  input  [3:0] ALU_op,
  output [31:0] ALUOut
);

  wire comparator_1_lt, comparator_2_lt, comparator_3_eq, comparator_3_gt, comparator_3_lt, not_1_out,
       or_2_out;
  wire [31:0] AddOut, AndOut, beq, bge, blt, bltu, bne, OrOut, SlaOut, SllOut, SltOut, SltuOut, SrlOut,
       SubOut, XorOut;

  Adder #(.width(32)) adder_1 (.a(DataA), .b(DataB), .out(AddOut));  // open: cin, cout
  assign XorOut = DataA ^ DataB;  // XOR_Gate xor_1, 32 bits wide
  Subtractor #(.width(32)) subtractor_1 (.a(DataA), .b(DataB), .out(SubOut));  // open: bin, bout
  Shifter #(.shift("lr"), .width(32)) shifter_1 (.in(DataA), .\dist (DataB[4:0]), .out(SrlOut));
  Shifter #(.width(32)) shifter_2 (.in(DataA), .\dist (DataB[4:0]), .out(SllOut));
  Shifter #(.shift("ar"), .width(32)) shifter_3 (.in(DataA), .\dist (DataB[4:0]), .out(SlaOut));
  Comparator #(.width(32)) comparator_1 (.a(DataA), .b(DataB), .lt(comparator_1_lt));  // open: gt, eq
  assign OrOut = DataA | DataB;  // OR_Gate or_1, 32 bits wide
  assign SltOut = {{31{1'b0}}, comparator_1_lt};  // Bit_Extender bit_extender_1
  Comparator #(.mode("unsigned"), .width(32)) comparator_2 (
    .a(DataA), .b(DataB), .lt(comparator_2_lt));  // open: gt, eq
  assign AndOut = DataA & DataB;  // AND_Gate and_1, 32 bits wide
  assign SltuOut = {{31{1'b0}}, comparator_2_lt};  // Bit_Extender bit_extender_2
  Multiplexer #(.select(4), .width(32)) multiplexer_1 (
    .in0(AddOut), .in1(SubOut), .in2(XorOut), .in3(OrOut), .in4(AndOut), .in5(SllOut), .in6(SltuOut),
    .in7(SltOut), .in8(beq), .in9(bne), .in10(blt), .in11(bge), .in12(bltu), .out(ALUOut), .sel(ALU_op));  // open: in13, in14, in15
  Comparator #(.width(32)) comparator_3 (
    .a(DataA), .b(DataB), .gt(comparator_3_gt), .eq(comparator_3_eq), .lt(comparator_3_lt));
  not not_1 (not_1_out, comparator_3_eq);
  assign beq = {{31{comparator_3_eq}}, comparator_3_eq};  // Bit_Extender bit_extender_3
  assign bne = {{31{not_1_out}}, not_1_out};  // Bit_Extender bit_extender_4
  assign blt = {{31{comparator_3_lt}}, comparator_3_lt};  // Bit_Extender bit_extender_5
  or or_2 (or_2_out, comparator_3_gt, comparator_3_eq);
  assign bge = {{31{or_2_out}}, or_2_out};  // Bit_Extender bit_extender_6
  assign bltu = {{31{comparator_3_lt}}, comparator_3_lt};  // Bit_Extender bit_extender_7
endmodule

module InstructionDecoder (
  input  [31:0] Instruction,
  output [31:0] Imm,
  output [4:0] rd,
  output [4:0] rs1,
  output [4:0] rs2,
  output [2:0] funct3,
  output [6:0] funct7,
  output [6:0] opcode
);

  wire [2:0] I_funct3, R_funct3, S_funct3, SB_funct3;
  wire [3:0] sbsplitter_1_imm4_1;
  wire [4:0] I_rd, I_rs1, R_rd, R_rs1, R_rs2, S_rs1, S_rs2, SB_rs1, SB_rs2, ssplitter_1_imm4_0;
  wire [5:0] sbsplitter_1_imm10_5;
  wire [6:0] I_opcode, R_funct7, R_opcode, S_opcode, SB_opcode, ssplitter_1_imm11_5;
  wire [11:0] isplitter_1_imm11_0, sbsplitter_1_imm11;
  wire [31:0] I_imm, S_imm, SB_imm;

  Isplitter isplitter_1 (
    .instruction(Instruction), .opcode(I_opcode), .rd(I_rd), .funct3(I_funct3), .rs1(I_rs1),
    .imm11_0(isplitter_1_imm11_0));
  assign I_imm = {{20{isplitter_1_imm11_0[11]}}, isplitter_1_imm11_0};  // Bit_Extender bit_extender_1
  Ssplitter ssplitter_1 (
    .instruction(Instruction), .opcode(S_opcode), .imm4_0(ssplitter_1_imm4_0), .funct3(S_funct3),
    .rs1(S_rs1), .rs2(S_rs2), .imm11_5(ssplitter_1_imm11_5));
  SBsplitter sbsplitter_1 (
    .instruction(Instruction), .opcode(SB_opcode), .imm11(sbsplitter_1_imm11[0]),
    .imm4_1(sbsplitter_1_imm4_1), .funct3(SB_funct3), .rs1(SB_rs1), .rs2(SB_rs2),
    .imm10_5(sbsplitter_1_imm10_5), .imm12(sbsplitter_1_imm11[11]));
  Rspitter rspitter_1 (
    .instruction(Instruction), .opcode(R_opcode), .rd(R_rd), .funct3(R_funct3), .rs1(R_rs1), .rs2(R_rs2),
    .funct7(R_funct7));
  assign S_imm = {{20{ssplitter_1_imm11_5[6]}}, {ssplitter_1_imm11_5, ssplitter_1_imm4_0}};  // Bit_Extender bit_extender_2
  assign SB_imm = {{20{sbsplitter_1_imm11[11]}}, {sbsplitter_1_imm11[11], sbsplitter_1_imm10_5, sbsplitter_1_imm4_1, sbsplitter_1_imm11[0]}};  // Bit_Extender bit_extender_3
  Multiplexer #(.select(3), .width(32)) multiplexer_1 (
    .in1(I_imm), .in2(S_imm), .in3({32{1'b0}}), .in6(SB_imm), .out(Imm), .sel(Instruction[2:0]));  // open: in0, in4, in5, in7
  Multiplexer #(.select(3), .width(5)) multiplexer_2 (
    .in1(I_rd), .in2({5{1'b0}}), .in3(R_rd), .in6({5{1'b0}}), .out(rd), .sel(Instruction[2:0]));  // open: in0, in4, in5, in7
  Multiplexer #(.select(3), .width(5)) multiplexer_3 (
    .in1(I_rs1), .in2(S_rs1), .in3(R_rs1), .in6(SB_rs1), .out(rs1), .sel(Instruction[2:0]));  // open: in0, in4, in5, in7
  Multiplexer #(.select(3), .width(5)) multiplexer_4 (
    .in1({5{1'b0}}), .in2(S_rs2), .in3(R_rs2), .in6(SB_rs2), .out(rs2), .sel(Instruction[2:0]));  // open: in0, in4, in5, in7
  Multiplexer #(.select(3), .width(3)) multiplexer_5 (
    .in1(I_funct3), .in2(S_funct3), .in3(R_funct3), .in6(SB_funct3), .out(funct3), .sel(Instruction[2:0]));  // open: in0, in4, in5, in7
  Multiplexer #(.select(3), .width(7)) multiplexer_6 (
    .in1({7{1'b0}}), .in2({7{1'b0}}), .in3(R_funct7), .in6({7{1'b0}}), .out(funct7), .sel(Instruction[2:0]));  // open: in0, in4, in5, in7
  Multiplexer #(.select(3), .width(7)) multiplexer_7 (
    .in1(I_opcode), .in2(S_opcode), .in3(R_opcode), .in6(SB_opcode), .out(opcode), .sel(Instruction[2:0]));  // open: in0, in4, in5, in7

  // Other names for the same wires on the sheet: sel[2:0] = Instruction[2:0]
endmodule

module Isplitter (
  input  [31:0] instruction,
  output [6:0] opcode,
  output [4:0] rd,
  output [2:0] funct3,
  output [4:0] rs1,
  output [11:0] imm11_0
);


  assign funct3 = instruction[14:12];
  assign imm11_0 = instruction[31:20];
  assign opcode = instruction[6:0];
  assign rd = instruction[11:7];
  assign rs1 = instruction[19:15];
endmodule

module Ssplitter (
  input  [31:0] instruction,
  output [6:0] opcode,
  output [4:0] imm4_0,
  output [2:0] funct3,
  output [4:0] rs1,
  output [4:0] rs2,
  output [6:0] imm11_5
);


  assign funct3 = instruction[14:12];
  assign imm4_0 = instruction[11:7];
  assign imm11_5 = instruction[31:25];
  assign opcode = instruction[6:0];
  assign rs1 = instruction[19:15];
  assign rs2 = instruction[24:20];
endmodule

module Rspitter (
  input  [31:0] instruction,
  output [6:0] opcode,
  output [4:0] rd,
  output [2:0] funct3,
  output [4:0] rs1,
  output [4:0] rs2,
  output [6:0] funct7
);


  assign funct3 = instruction[14:12];
  assign funct7 = instruction[31:25];
  assign opcode = instruction[6:0];
  assign rd = instruction[11:7];
  assign rs1 = instruction[19:15];
  assign rs2 = instruction[24:20];
endmodule

module SBsplitter (
  input  [31:0] instruction,
  output [6:0] opcode,
  output imm11,
  output [3:0] imm4_1,
  output [2:0] funct3,
  output [4:0] rs1,
  output [4:0] rs2,
  output [5:0] imm10_5,
  output imm12
);


  assign funct3 = instruction[14:12];
  assign imm4_1 = instruction[11:8];
  assign imm10_5 = instruction[30:25];
  assign imm11 = instruction[7];
  assign imm12 = instruction[31];
  assign opcode = instruction[6:0];
  assign rs1 = instruction[19:15];
  assign rs2 = instruction[24:20];
endmodule

module BranchPredictionUnit (
  input  [31:0] currentPC,
  input  [31:0] imm,
  input  [31:0] rs2,
  input  [31:0] rs1,
  input  branch,
  input  clk,
  input  [2:0] funct3,
  output [31:0] destAddr
);

  wire and_1_out, and_2_out, and_3_out, beq_out, bge_out, bgeu_out, blt_out, bltu_out, bne_out, CV, d_ff_1_q,
       d_ff_2_q, d_ff_2_qn, Igual, Maior, Menor, multiplexer_1_out, multiplexer_3_out, multiplexer_4_out,
       multiplexer_5_out, multiplexer_6_out, multiplexer_7_out, not_1_out, not_2_out, not_3_out, not_4_out,
       not_5_out, not_6_out, not_7_out, not_8_out, not_9_out, not_10_out, or_1_out, or_2_out, or_3_out;
  wire [31:0] adder_1_out, adder_2_out;

  Comparator #(.width(32)) comparator_1 (.a(rs2), .b(rs1), .gt(Maior), .eq(Igual), .lt(Menor));
  and and_1 (and_1_out, CV, branch);
  not not_1 (not_1_out, funct3[0]);
  not not_2 (not_2_out, funct3[1]);
  and beq (beq_out, not_1_out, not_2_out, not_3_out);
  Adder #(.width(32)) adder_1 (.a(currentPC), .b(imm), .out(adder_1_out));  // open: cin, cout
  Adder #(.width(32)) adder_2 (.a(imm), .b(32'h4), .out(adder_2_out));  // open: cin, cout
  not not_3 (not_3_out, funct3[2]);
  Multiplexer multiplexer_1 (.in0(1'b0), .in1(Igual), .out(multiplexer_1_out), .sel(beq_out));
  Multiplexer #(.width(32)) multiplexer_2 (.in0(adder_1_out), .in1(adder_2_out), .out(destAddr), .sel(d_ff_1_q));
  and and_2 (and_2_out, d_ff_2_q, and_1_out);
  not not_4 (not_4_out, funct3[1]);
  not not_5 (not_5_out, funct3[2]);
  and bne (bne_out, funct3[0], not_4_out, not_5_out);
  not not_6 (not_6_out, Igual);
  Multiplexer multiplexer_3 (.in0(1'b0), .in1(not_6_out), .out(multiplexer_3_out), .sel(bne_out));
  or or_1 (or_1_out, d_ff_1_q, and_2_out);
  and and_3 (and_3_out, d_ff_2_qn, and_1_out);
  not not_7 (not_7_out, funct3[0]);
  not not_8 (not_8_out, funct3[1]);
  and blt (blt_out, not_7_out, not_8_out, funct3[2]);
  D_Flip_Flop d_ff_1 (.D(or_1_out), .clk(clk), .Q(d_ff_1_q));  // open: Qn, preset, reset
  D_Flip_Flop d_ff_2 (.D(and_3_out), .clk(clk), .Q(d_ff_2_q), .Qn(d_ff_2_qn));  // open: preset, reset
  not not_9 (not_9_out, funct3[1]);
  and bge (bge_out, funct3[0], not_9_out, funct3[2]);
  Multiplexer multiplexer_4 (.in0(1'b0), .in1(Menor), .out(multiplexer_4_out), .sel(blt_out));
  or or_2 (or_2_out, Maior, Igual);
  Multiplexer multiplexer_5 (.in0(1'b0), .in1(or_2_out), .out(multiplexer_5_out), .sel(bge_out));
  and bgeu (bgeu_out, funct3[0], funct3[1], funct3[2]);
  or or_3 (or_3_out, Maior, Igual);
  Multiplexer multiplexer_6 (.in0(1'b0), .in1(or_3_out), .out(multiplexer_6_out), .sel(bgeu_out));
  not not_10 (not_10_out, funct3[2]);
  and bltu (bltu_out, not_10_out, funct3[1], funct3[0]);
  Multiplexer multiplexer_7 (.in0(1'b0), .in1(Menor), .out(multiplexer_7_out), .sel(bltu_out));
  or or_4 (CV, multiplexer_7_out, multiplexer_6_out, multiplexer_5_out, multiplexer_4_out, multiplexer_3_out, multiplexer_1_out);

  // Other names for the same wires on the sheet: rs1_t[31:0] = rs2; rs2_t[31:0] = rs1

  // Notes on the sheet:
  //   targetAddr
  //   nextAddr
  //   return the destiny address to the branch instruction
  //   Condição verdadeira
endmodule

module ControlUnit (
  input  [31:0] instruction2Type,
  input  [31:0] instruction1Type,
  output regWriteALU,
  output regWriteMem,
  output memWrite,
  output memRead,
  output ALUSrc_arithm,
  output ALUSrc_mem,
  output [3:0] ALUOp_arithm,
  output [3:0] ALUOp_mem,
  output branch,
  output inst1Mem
);

  wire Add_out, Addi_out, andd_out, beq_out, bge_out, blt_out, bltu_out, bne_out, not_1_out, not_2_out,
       not_3_out, not_4_out, not_5_out, not_6_out, not_7_out, not_8_out, not_9_out, not_10_out, not_11_out,
       not_12_out, not_13_out, not_14_out, not_15_out, not_16_out, not_17_out, not_18_out, not_19_out,
       not_20_out, not_21_out, not_22_out, not_23_out, not_24_out, not_25_out, not_26_out, not_27_out,
       not_28_out, not_29_out, not_30_out, not_31_out, not_32_out, not_33_out, not_34_out, not_35_out,
       not_36_out, not_37_out, not_38_out, not_39_out, not_40_out, not_41_out, not_42_out, not_43_out,
       not_44_out, not_45_out, not_46_out, not_47_out, not_48_out, not_49_out, not_50_out, not_51_out,
       not_52_out, not_53_out, not_54_out, not_55_out, oor_out, or_4_out, or_5_out, or_6_out, SinalLW,
       SinalR, slll_out, slti_out, sltu_out, sub_out, TipoB, TipoI, TipoS, xoor_out;
  wire [3:0] AluB, AluI, AluLWM, AluR, AluSWM, multiplexer_1_out, multiplexer_2_out, multiplexer_3_out,
       multiplexer_4_out, multiplexer_5_out, multiplexer_6_out, multiplexer_7_out, multiplexer_8_out,
       multiplexer_9_out, multiplexer_10_out, multiplexer_11_out, multiplexer_14_out, multiplexer_15_out,
       or_1_out, or_2_out, or_3_out;

  not not_1 (not_1_out, instruction1Type[2]);
  not not_2 (not_2_out, instruction1Type[3]);
  not not_3 (not_3_out, instruction1Type[6]);
  not not_4 (not_4_out, instruction1Type[2]);
  not not_5 (not_5_out, instruction1Type[3]);
  not not_6 (not_6_out, instruction1Type[4]);
  not not_7 (not_7_out, instruction1Type[2]);
  not not_8 (not_8_out, instruction1Type[3]);
  not not_9 (not_9_out, instruction1Type[4]);
  not not_10 (not_10_out, instruction1Type[6]);
  not not_11 (not_11_out, instruction1Type[2]);
  not not_12 (not_12_out, instruction1Type[3]);
  not not_13 (not_13_out, instruction1Type[5]);
  not not_14 (not_14_out, instruction1Type[6]);
  not not_15 (not_15_out, instruction1Type[2]);
  not not_16 (not_16_out, instruction1Type[3]);
  not not_17 (not_17_out, instruction1Type[4]);
  not not_18 (not_18_out, instruction1Type[6]);
  not not_19 (not_19_out, instruction1Type[12]);
  not not_20 (not_20_out, instruction1Type[13]);
  not not_21 (not_21_out, instruction1Type[14]);
  not not_22 (not_22_out, instruction1Type[25]);
  not not_23 (not_23_out, instruction1Type[26]);
  and Add (Add_out, not_19_out, not_20_out, not_21_out, not_22_out, not_23_out, not_24_out, not_25_out, not_26_out, not_27_out, not_28_out);
  not not_24 (not_24_out, instruction1Type[27]);
  not not_25 (not_25_out, instruction1Type[28]);
  not not_26 (not_26_out, instruction1Type[29]);
  not not_27 (not_27_out, instruction1Type[30]);
  not not_28 (not_28_out, instruction1Type[31]);
  not not_29 (not_29_out, instruction1Type[12]);
  not not_30 (not_30_out, instruction1Type[13]);
  not not_31 (not_31_out, instruction1Type[14]);
  not not_32 (not_32_out, instruction1Type[25]);
  and sub (sub_out, not_29_out, not_30_out, not_31_out, not_32_out, instruction1Type[26], not_33_out, not_34_out, not_35_out, not_36_out, not_37_out);
  not not_33 (not_33_out, instruction1Type[27]);
  not not_34 (not_34_out, instruction1Type[28]);
  not not_35 (not_35_out, instruction1Type[29]);
  not not_36 (not_36_out, instruction1Type[30]);
  not not_37 (not_37_out, instruction1Type[31]);
  not not_38 (not_38_out, instruction1Type[12]);
  not not_39 (not_39_out, instruction1Type[13]);
  and xoor (xoor_out, not_38_out, not_39_out, instruction1Type[14]);
  not not_40 (not_40_out, instruction1Type[12]);
  and oor (oor_out, not_40_out, instruction1Type[13], instruction1Type[14]);
  and andd (andd_out, instruction1Type[12], instruction1Type[13], instruction1Type[14]);
  not not_41 (not_41_out, instruction1Type[13]);
  and slll (slll_out, instruction1Type[12], not_41_out, not_42_out);
  not not_42 (not_42_out, instruction1Type[14]);
  and sltu (sltu_out, instruction1Type[12], instruction1Type[13], not_43_out);
  not not_43 (not_43_out, instruction1Type[14]);
  and R (SinalR, instruction1Type[0], instruction1Type[1], not_1_out, not_2_out, instruction1Type[4], instruction1Type[5], not_3_out);
  and B (TipoB, instruction1Type[0], instruction1Type[1], not_4_out, not_5_out, not_6_out, instruction1Type[5], instruction1Type[6]);
  not not_44 (not_44_out, instruction1Type[12]);
  not not_45 (not_45_out, instruction1Type[13]);
  and beq (beq_out, not_44_out, not_45_out, not_46_out);
  not not_46 (not_46_out, instruction1Type[14]);
  not not_47 (not_47_out, instruction1Type[13]);
  and bne (bne_out, instruction1Type[12], not_47_out, not_48_out);
  not not_48 (not_48_out, instruction1Type[14]);
  not not_49 (not_49_out, instruction1Type[12]);
  not not_50 (not_50_out, instruction1Type[13]);
  and blt (blt_out, not_49_out, not_50_out, instruction1Type[14]);
  not not_51 (not_51_out, instruction1Type[13]);
  and bge (bge_out, instruction1Type[12], not_51_out, instruction1Type[14]);
  and bltu (bltu_out, instruction1Type[12], instruction1Type[13], not_52_out);
  not not_52 (not_52_out, instruction1Type[14]);
  and u_TipoS (TipoS, instruction1Type[0], instruction1Type[1], not_7_out, not_8_out, not_9_out, instruction1Type[5], not_10_out);
  and u_TipoI (TipoI, instruction1Type[0], instruction1Type[1], not_11_out, not_12_out, instruction1Type[4], not_13_out, not_14_out);
  not not_53 (not_53_out, instruction1Type[12]);
  and slti (slti_out, not_53_out, instruction1Type[13], not_54_out);
  not not_54 (not_54_out, instruction1Type[14]);
  and LW (SinalLW, instruction1Type[0], instruction1Type[1], not_15_out, not_16_out, not_17_out, instruction1Type[5], not_18_out);
  not not_55 (not_55_out, slti_out);
  Multiplexer #(.width(4)) multiplexer_1 (.in0(4'b0000), .in1(4'b0001), .out(multiplexer_1_out), .sel(sub_out));
  Multiplexer #(.width(4)) multiplexer_2 (.in0(4'b0000), .in1(4'b0010), .out(multiplexer_2_out), .sel(xoor_out));
  Multiplexer #(.width(4)) multiplexer_3 (.in0(4'b0000), .in1(4'b0011), .out(multiplexer_3_out), .sel(oor_out));
  Multiplexer #(.width(4)) multiplexer_4 (.in0(4'b0000), .in1(4'b0100), .out(multiplexer_4_out), .sel(andd_out));
  Multiplexer #(.width(4)) multiplexer_5 (.in0(4'b0000), .in1(4'b0101), .out(multiplexer_5_out), .sel(slll_out));
  Multiplexer #(.width(4)) multiplexer_6 (.in0(4'b0000), .in1(4'b0110), .out(multiplexer_6_out), .sel(sltu_out));
  Multiplexer #(.width(4)) multiplexer_7 (.in0(4'b0000), .in1(4'b1001), .out(multiplexer_7_out), .sel(beq_out));
  Multiplexer #(.width(4)) multiplexer_8 (.in0(4'b0000), .in1(4'b1010), .out(multiplexer_8_out), .sel(bne_out));
  Multiplexer #(.width(4)) multiplexer_9 (.in0(4'b0000), .in1(4'b1011), .out(multiplexer_9_out), .sel(blt_out));
  Multiplexer #(.width(4)) multiplexer_10 (.in0(4'b0000), .in1(4'b1100), .out(multiplexer_10_out), .sel(bge_out));
  Multiplexer #(.width(4)) multiplexer_11 (.in0(4'b0000), .in1(4'b1101), .out(multiplexer_11_out), .sel(bltu_out));
  Multiplexer #(.width(4)) multiplexer_12 (.in0(4'b0000), .in1(4'b0010), .out(AluSWM), .sel(TipoS));
  and Addi (Addi_out, TipoI, not_55_out);
  Multiplexer #(.width(4)) multiplexer_13 (.in0(4'b0000), .in1(4'b0001), .out(AluLWM), .sel(SinalLW));
  assign or_1_out = multiplexer_7_out | multiplexer_8_out | multiplexer_9_out | multiplexer_10_out | multiplexer_11_out;  // OR_Gate or_1, 4 bits wide
  Multiplexer #(.width(4)) multiplexer_14 (.in0(4'b0000), .in1(4'b0000), .out(multiplexer_14_out), .sel(Addi_out));
  Multiplexer #(.width(4)) multiplexer_15 (.in0(4'b0000), .in1(4'b1000), .out(multiplexer_15_out), .sel(slti_out));
  assign or_2_out = 4'b0000 | multiplexer_1_out | multiplexer_2_out | multiplexer_3_out | multiplexer_4_out | multiplexer_5_out | multiplexer_6_out;  // OR_Gate or_2, 4 bits wide
  Multiplexer #(.width(4)) multiplexer_16 (.in0(4'b0000), .in1(or_1_out), .out(AluB), .sel(TipoB));
  assign or_3_out = multiplexer_14_out | multiplexer_15_out;  // OR_Gate or_3, 4 bits wide
  Multiplexer #(.width(4)) multiplexer_17 (.in0(4'b0000), .in1(or_2_out), .out(AluR), .sel(SinalR));
  Multiplexer #(.width(4)) multiplexer_18 (.in0(4'b0000), .in1(or_3_out), .out(AluI), .sel(TipoI));
  or or_4 (or_4_out, TipoI, SinalR);
  or or_5 (or_5_out, SinalLW, TipoS);
  or or_6 (or_6_out, SinalLW, TipoS);
  and and_1 (regWriteALU, 1'b1, or_4_out);
  and and_2 (regWriteMem, 1'b1, SinalLW);
  and and_3 (memWrite, 1'b1, TipoS);
  and and_4 (memRead, 1'b1, SinalLW);
  and and_5 (ALUSrc_arithm, 1'b1, TipoI);
  and and_6 (ALUSrc_mem, 1'b1, or_5_out);
  assign ALUOp_arithm = AluR | AluI | AluB;  // OR_Gate or_7, 4 bits wide
  assign ALUOp_mem = AluSWM | 4'b0000 | AluLWM;  // OR_Gate or_8, 4 bits wide
  and and_7 (branch, 1'b1, TipoB);
  and and_8 (inst1Mem, 1'b1, or_6_out);

  // Notes on the sheet:
  //   1 WE to arithmetic operation / 0 not WE
  //   1 to mem write operation / 0 not
  //   1 to mem read operation / 0 not
  //   1 WE to mem access operation / 0 not WE
  //   1 immediate used on arithmetic instruction / 0 register used
  //   1 immediate used on mem access instruction / 0 register used
  //   Instruction arithmetic operation code to ULA
  //   Instruction mem operation code to ULA
  //   1 the arithmetic instruction is branch / 0 is not branch
  //   1 first instruction represents memory access / 0 first instruction represents arithmetic operations
endmodule
