// Logisim project RegistersSet.circ as structural Verilog: 1 circuit, main circuit main
module main (
  input  [31:0] rd_out,
  input  [31:0] rs1_out,
  input  [4:0] rs1_ref,
  input  [4:0] rd_ref,
  input  [31:0] rs2_out,
  input  [4:0] rs2_ref,
  input  WE
);

  wire clk, WE_0, WE_1, WE_2, WE_3, WE_4, WE_5, WE_7, WE_8, WE_9, WE_10, WE_11, WE_12, WE_14, WE_15, WE_16,
       WE_17, WE_18, WE_20, WE_21, WE_22, WE_23, WE_24, WE_25, WE_26, WE_27, WE_28, WE_29, WE_30, WE_31;
  wire [31:0] RSq_1, RSq_2, RSq_3, RSq_4, RSq_5, RSq_6, RSq_7, RSq_8, RSq_9, RSq_10, RSq_11, RSq_12, RSq_13,
       RSq_14, RSq_15, RSq_16, RSq_17, RSq_18, RSq_19, RSq_20, RSq_21, RSq_22, RSq_23, RSq_24, RSq_25,
       RSq_26, RSq_27, RSq_28, RSq_29, RSq_30, RSq_31;

  Multiplexer #(.select(5), .width(32), .enable("false")) multiplexer_1 (
    .in0({32{1'b0}}), .in1(RSq_1), .in2(RSq_2), .in3(RSq_3), .in4(RSq_4), .in5(RSq_5), .in6(RSq_6),
    .in7(RSq_7), .in8(RSq_8), .in9(RSq_9), .in10(RSq_10), .in11(RSq_11), .in12(RSq_12), .in13(RSq_13),
    .in14(RSq_14), .in15(RSq_15), .in16(RSq_16), .in17(RSq_17), .in18(RSq_18), .in19(RSq_19), .in20(RSq_20),
    .in21(RSq_21), .in22(RSq_22), .in23(RSq_23), .in24(RSq_24), .in25(RSq_25), .in26(RSq_26), .in27(RSq_27),
    .in28(RSq_28), .in29(RSq_29), .in30(RSq_30), .in31(RSq_31), .out(rs1_out), .sel(rs1_ref));
  Multiplexer #(.select(5), .width(32), .enable("false")) multiplexer_2 (
    .in0({32{1'b0}}), .in1(RSq_1), .in2(RSq_2), .in3(RSq_3), .in4(RSq_4), .in5(RSq_5), .in6(RSq_6),
    .in7(RSq_7), .in8(RSq_8), .in9(RSq_9), .in10(RSq_10), .in11(RSq_11), .in12(RSq_12), .in13(RSq_13),
    .in14(RSq_14), .in15(RSq_15), .in16(RSq_16), .in17(RSq_17), .in18(RSq_18), .in19(RSq_19), .in20(RSq_20),
    .in21(RSq_21), .in22(RSq_22), .in23(RSq_23), .in24(RSq_24), .in25(RSq_25), .in26(RSq_26), .in27(RSq_27),
    .in28(RSq_28), .in29(RSq_29), .in30(RSq_30), .in31(RSq_31), .out(rs2_out), .sel(rs2_ref));
  Register #(.width(32), .Select("low")) _4 (.D(rd_out), .en(WE_4), .Q(RSq_4), .clk(clk));  // open: clr
  Register #(.width(32), .Select("low")) _8 (.D(rd_out), .en(WE_8), .Q(RSq_8), .clk(clk));  // open: clr
  Register #(.width(32), .Select("low")) _12 (.D(rd_out), .en(WE_12), .Q(RSq_12), .clk(clk));  // open: clr
  Register #(.width(32), .Select("low")) _16 (.D(rd_out), .en(WE_16), .Q(RSq_16), .clk(clk));  // open: clr
  Register #(.width(32), .Select("low")) _20 (.D(rd_out), .en(WE_20), .Q(RSq_20), .clk(clk));  // open: clr
  Register #(.width(32), .Select("low")) _24 (.D(rd_out), .en(WE_24), .Q(RSq_24), .clk(clk));  // open: clr
  Register #(.width(32), .Select("low")) _28 (.D(rd_out), .en(WE_28), .Q(RSq_28), .clk(clk));  // open: clr
  Register #(.width(32), .Select("low")) _1 (.D(rd_out), .en(WE_1), .Q(RSq_1), .clk(clk));  // open: clr
  Register #(.width(32), .Select("low")) _5 (.D(rd_out), .en(WE_5), .Q(RSq_5), .clk(clk));  // open: clr
  Register #(.width(32), .Select("low")) _9 (.D(rd_out), .en(WE_9), .Q(RSq_9), .clk(clk));  // open: clr
  Register #(.width(32), .Select("low")) _13 (.D(rd_out), .en(WE_12), .Q(RSq_13), .clk(clk));  // open: clr
  Register #(.width(32), .Select("low")) _17 (.D(rd_out), .en(WE_17), .Q(RSq_17), .clk(clk));  // open: clr
  Register #(.width(32), .Select("low")) _21 (.D(rd_out), .en(WE_21), .Q(RSq_21), .clk(clk));  // open: clr
  Register #(.width(32), .Select("low")) _25 (.D(rd_out), .en(WE_25), .Q(RSq_25), .clk(clk));  // open: clr
  Register #(.width(32), .Select("low")) _29 (.D(rd_out), .en(WE_29), .Q(RSq_29), .clk(clk));  // open: clr
  Register #(.width(32), .Select("low")) _2 (.D(rd_out), .en(WE_2), .Q(RSq_2), .clk(clk));  // open: clr
  Register #(.width(32), .Select("low")) _6 (.D(rd_out), .en(WE_5), .Q(RSq_6), .clk(clk));  // open: clr
  Register #(.width(32), .Select("low")) _10 (.D(rd_out), .en(WE_10), .Q(RSq_10), .clk(clk));  // open: clr
  Register #(.width(32), .Select("low")) _14 (.D(rd_out), .en(WE_14), .Q(RSq_14), .clk(clk));  // open: clr
  Register #(.width(32), .Select("low")) _18 (.D(rd_out), .en(WE_18), .Q(RSq_18), .clk(clk));  // open: clr
  Register #(.width(32), .Select("low")) _22 (.D(rd_out), .en(WE_22), .Q(RSq_22), .clk(clk));  // open: clr
  Register #(.width(32), .Select("low")) _26 (.D(rd_out), .en(WE_26), .Q(RSq_26), .clk(clk));  // open: clr
  Register #(.width(32), .Select("low")) _30 (.D(rd_out), .en(WE_30), .Q(RSq_30), .clk(clk));  // open: clr
  Register #(.width(32), .Select("low")) _3 (.D(rd_out), .en(WE_3), .Q(RSq_3), .clk(clk));  // open: clr
  Register #(.width(32), .Select("low")) _7 (.D(rd_out), .en(WE_7), .Q(RSq_7), .clk(clk));  // open: clr
  Register #(.width(32), .Select("low")) _11 (.D(rd_out), .en(WE_11), .Q(RSq_11), .clk(clk));  // open: clr
  Register #(.width(32), .Select("low")) _15 (.D(rd_out), .en(WE_15), .Q(RSq_15), .clk(clk));  // open: clr
  Register #(.width(32), .Select("low")) _19 (.D(rd_out), .en(WE_12), .Q(RSq_19), .clk(clk));  // open: clr
  Register #(.width(32), .Select("low")) _23 (.D(rd_out), .en(WE_23), .Q(RSq_23), .clk(clk));  // open: clr
  Register #(.width(32), .Select("low")) _27 (.D(rd_out), .en(WE_27), .Q(RSq_27), .clk(clk));  // open: clr
  Register #(.width(32), .Select("low")) _31 (.D(rd_out), .en(WE_31), .Q(RSq_31), .clk(clk));  // open: clr
  Demultiplexer #(.select(5), .enable("false")) demultiplexer_1 (
    .out0(WE_0), .out1(WE_1), .out2(WE_2), .out3(WE_3), .out4(WE_4), .out5(WE_5), .out6(WE_5), .out7(WE_7),
    .out8(WE_8), .out9(WE_9), .out10(WE_10), .out11(WE_11), .out12(WE_12), .out13(WE_12), .out14(WE_14),
    .out15(WE_15), .out16(WE_16), .out17(WE_17), .out18(WE_18), .out19(WE_12), .out20(WE_20), .out21(WE_21),
    .out22(WE_22), .out23(WE_23), .out24(WE_24), .out25(WE_25), .out26(WE_26), .out27(WE_27), .out28(WE_28),
    .out29(WE_29), .out30(WE_30), .out31(WE_31), .in(WE), .sel(rd_ref));
  Clock clock_1 (.out(clk));

  // Other names for the same wires on the sheet: WE_6 = WE_5; WE_13 = WE_12; WE_19 = WE_12

  // Notes on the sheet:
  //   Registers set (32).
  //   Foreign signals.
  //   Select the RD to enable the write.
endmodule
