// Digital circuit SEMÁFORO 2 (MOORE).dig as structural Verilog
module \SEMÁFORO_2__MOORE  (
  input  EA1,
  input  EA1N,
  input  EA2,
  input  EA2N,
  input  EA3,
  input  EA3N,
  output VERDE,
  output AMARELO,
  output VERMELHO
);

  wire and_1_out, and_2_out, and_3_out;

  and and_1 (and_1_out, EA1, EA3);
  and and_2 (and_2_out, EA2, EA3, EA1N);
  and and_3 (and_3_out, EA3N, EA2, EA1);
  or or_1 (AMARELO, and_2_out, and_3_out);
  and and_4 (VERDE, EA3N, EA2, EA1N);
  or or_2 (VERMELHO, and_1_out, EA2N);
endmodule
