// Digital circuit SEMÁFOROS 1 E 3 (MOORE).dig as structural Verilog
module \SEMÁFOROS_1_E_3__MOORE  (
  input  EA1,
  input  EA1N,
  input  EA2,
  input  EA2N,
  input  EA3,
  input  EA3N,
  output VERDE,
  output AMARELO,
  output VERMELHO
);

  wire and_2_out, and_3_out, and_4_out;

  and and_1 (VERDE, EA1N, EA2N, EA3N);
  and and_2 (and_2_out, EA1N, EA2N, EA3);
  and and_3 (and_3_out, EA1, EA2N, EA3N);
  and and_4 (and_4_out, EA1, EA3);
  or or_1 (AMARELO, and_2_out, and_3_out);
  or or_2 (VERMELHO, and_4_out, EA2);
endmodule
