// Digital circuit SEMÁFOROS 4 E 5 (MOORE).dig as structural Verilog
module \SEMÁFOROS_4_E_5__MOORE  (
  input  EA1,
  input  EA3,
  output VERMELHO,
  output VERDE
);

  and and_1 (VERDE, EA1, EA3);
  not not_1 (VERMELHO, VERDE);
endmodule
