// Digital circuit SEMÁFOROS MOORE.dig as structural Verilog
module \SEMÁFOROS_MOORE  (
  input  CLK
);

  wire and_1_out, and_2_out, and_3_out, and_4_out, and_5_out, and_6_out, and_7_out, and_8_out, and_9_out,
       and_10_out, button_1_out, d_ff_1_nq, d_ff_1_q, d_ff_2_nq, d_ff_2_q, d_ff_3_nq, d_ff_3_q, not_1_out,
       not_2_out, or_1_out, or_2_out, or_3_out, rs_ff_as_1_q, \semáforo_2__moore_1_amarelo ,
       \semáforo_2__moore_1_verde , \semáforo_2__moore_1_vermelho , \semáforos_1_e_3__moore_1_amarelo ,
       \semáforos_1_e_3__moore_1_verde , \semáforos_1_e_3__moore_1_vermelho ,
       \semáforos_1_e_3__moore_2_amarelo , \semáforos_1_e_3__moore_2_verde ,
       \semáforos_1_e_3__moore_2_vermelho , \semáforos_4_e_5__moore_1_verde ,
       \semáforos_4_e_5__moore_1_vermelho , \semáforos_4_e_5__moore_2_verde ,
       \semáforos_4_e_5__moore_2_vermelho ;

  Button button_1 (.out(button_1_out));
  RS_FF_AS rs_ff_as_1 (.S(button_1_out), .R(and_10_out), .Q(rs_ff_as_1_q));  // open: nQ
  not not_1 (not_1_out, rs_ff_as_1_q);
  not not_2 (not_2_out, rs_ff_as_1_q);
  and and_1 (and_1_out, rs_ff_as_1_q, d_ff_1_nq);
  and and_2 (and_2_out, d_ff_1_q, d_ff_3_nq);
  and and_3 (and_3_out, not_1_out, d_ff_2_nq, d_ff_3_q);
  and and_4 (and_4_out, rs_ff_as_1_q, d_ff_1_nq, d_ff_2_q);
  and and_5 (and_5_out, d_ff_1_q, d_ff_2_nq, d_ff_3_q);
  and and_6 (and_6_out, d_ff_2_q, d_ff_3_nq);
  and and_7 (and_7_out, not_2_out, d_ff_3_nq);
  and and_8 (and_8_out, rs_ff_as_1_q, d_ff_1_nq, d_ff_3_q);
  and and_9 (and_9_out, d_ff_1_q, d_ff_3_nq);
  or or_1 (or_1_out, and_3_out, and_4_out, and_5_out, and_6_out);
  or or_2 (or_2_out, and_7_out, and_8_out, and_9_out);
  or or_3 (or_3_out, and_1_out, and_2_out);
  and and_10 (and_10_out, \semáforos_4_e_5__moore_2_verde , \semáforos_4_e_5__moore_1_verde );
  D_FF d_ff_1 (.D(or_3_out), .C(CLK), .Q(d_ff_1_q), .nQ(d_ff_1_nq));
  D_FF d_ff_2 (.D(or_1_out), .C(CLK), .Q(d_ff_2_q), .nQ(d_ff_2_nq));
  D_FF d_ff_3 (.D(or_2_out), .C(CLK), .Q(d_ff_3_q), .nQ(d_ff_3_nq));
  \SEMÁFOROS_1_E_3__MOORE  \semáforos_1_e_3__moore_1  (
    .EA1(d_ff_1_q), .EA1N(d_ff_1_nq), .EA2(d_ff_2_q), .EA2N(d_ff_2_nq), .EA3(d_ff_3_q), .EA3N(d_ff_3_nq),
    .VERDE(\semáforos_1_e_3__moore_1_verde ), .AMARELO(\semáforos_1_e_3__moore_1_amarelo ),
    .VERMELHO(\semáforos_1_e_3__moore_1_vermelho ));
  \SEMÁFORO_2__MOORE  \semáforo_2__moore_1  (
    .EA1(d_ff_1_q), .EA1N(d_ff_1_nq), .EA2(d_ff_2_q), .EA2N(d_ff_2_nq), .EA3(d_ff_3_q), .EA3N(d_ff_3_nq),
    .VERDE(\semáforo_2__moore_1_verde ), .AMARELO(\semáforo_2__moore_1_amarelo ),
    .VERMELHO(\semáforo_2__moore_1_vermelho ));
  \SEMÁFOROS_1_E_3__MOORE  \semáforos_1_e_3__moore_2  (
    .EA1(d_ff_1_q), .EA1N(d_ff_1_nq), .EA2(d_ff_2_q), .EA2N(d_ff_2_nq), .EA3(d_ff_3_q), .EA3N(d_ff_3_nq),
    .VERDE(\semáforos_1_e_3__moore_2_verde ), .AMARELO(\semáforos_1_e_3__moore_2_amarelo ),
    .VERMELHO(\semáforos_1_e_3__moore_2_vermelho ));
  LED led_1 (.in(\semáforos_1_e_3__moore_1_verde ));
  LED led_2 (.in(\semáforos_1_e_3__moore_1_amarelo ));
  LED led_3 (.in(\semáforo_2__moore_1_verde ));
  LED led_4 (.in(\semáforo_2__moore_1_amarelo ));
  LED led_5 (.in(\semáforos_1_e_3__moore_2_verde ));
  LED led_6 (.in(\semáforos_1_e_3__moore_1_vermelho ));
  \SEMÁFOROS_4_E_5__MOORE  \semáforos_4_e_5__moore_1  (
    .EA1(d_ff_1_q), .EA3(d_ff_3_q), .VERMELHO(\semáforos_4_e_5__moore_1_vermelho ),
    .VERDE(\semáforos_4_e_5__moore_1_verde ));
  LED led_7 (.in(\semáforo_2__moore_1_vermelho ));
  \SEMÁFOROS_4_E_5__MOORE  \semáforos_4_e_5__moore_2  (
    .EA1(d_ff_1_q), .EA3(d_ff_3_q), .VERMELHO(\semáforos_4_e_5__moore_2_vermelho ),
    .VERDE(\semáforos_4_e_5__moore_2_verde ));
  LED led_8 (.in(\semáforos_1_e_3__moore_2_amarelo ));
  LED led_9 (.in(\semáforos_1_e_3__moore_2_vermelho ));
  LED led_10 (.in(\semáforos_4_e_5__moore_1_vermelho ));
  LED led_11 (.in(\semáforos_4_e_5__moore_2_vermelho ));
  LED led_12 (.in(\semáforos_4_e_5__moore_1_verde ));
  LED led_13 (.in(\semáforos_4_e_5__moore_2_verde ));
endmodule
