// Digital circuit ULA.dig as structural Verilog
module ULA (
  input  [31:0] A,
  input  [31:0] B,
  input  [2:0] fun,
  output [31:0] C
);

  wire comparator_1_eq, comparator_1_gt, comparator_1_lt;
  wire [31:0] add, \and , mul, \not , \or , slt, sub, \xor ;
  wire [63:32] mul_1_mul;

  Comparator #(.Bits(32), .Signed("true")) comparator_1 (
    .a(A), .b(B), .gt(comparator_1_gt), .eq(comparator_1_eq), .lt(comparator_1_lt));
  Add #(.Bits(32)) add_1 (.a(A), .b(B), .c_i(1'b0), .s(add));  // open: c_o
  Sub #(.Bits(32)) sub_1 (.a(A), .b(B), .c_i(1'b0), .s(sub));  // open: c_o
  Mul #(.Bits(32)) mul_1 (.a(A), .b(B), .mul({mul_1_mul, mul}));
  assign \and  = A & B;  // And and_1, 32 bits wide
  assign \or  = A | B;  // Or or_1, 32 bits wide
  assign \xor  = A ^ B;  // XOr xor_1, 32 bits wide
  BitExtender #(.inputBits(1), .outputBits(32)) bitextender_1 (.in(comparator_1_lt), .out(slt));
  assign \not  = ~A;  // Not not_1, 32 bits wide
  // Probe on mul_1_mul
  // Probe on comparator_1_gt
  // Probe on comparator_1_eq
  Multiplexer #(.Bits(32), .Selector_Bits(3)) multiplexer_1 (
    .sel(fun), .in_0(add), .in_1(sub), .in_2(mul), .in_3(\and ), .in_4(\or ), .in_5(\xor ), .in_6(slt),
    .in_7(\not ), .out(C));

  // Notes on the sheet:
  //   fun: Seletor de resultado da operação a ser gravado 
  //   no registrador C
endmodule
