// Digital circuit bRegs.dig as structural Verilog
module bRegs (
  input  [31:0] C,
  input  clk,
  input  [3:0] a_2,
  input  [3:0] b_2,
  input  [3:0] c_2,
  input  escR,
  output [31:0] A,
  output [31:0] B
);

  wire demultiplexer_1_out_0, demultiplexer_1_out_1, demultiplexer_1_out_2, demultiplexer_1_out_3,
       demultiplexer_1_out_4, demultiplexer_1_out_5, demultiplexer_1_out_6, demultiplexer_1_out_7,
       demultiplexer_1_out_8, demultiplexer_1_out_9, demultiplexer_1_out_10, demultiplexer_1_out_11,
       demultiplexer_1_out_12, demultiplexer_1_out_13, demultiplexer_1_out_14, demultiplexer_1_out_15;
  wire [31:0] R0, R1, R2, R3, R4, R5, R6, R7, R8, R9, R10, R11, R12, R13, R14, R15;

  Demultiplexer #(.Selector_Bits(4)) demultiplexer_1 (
    .sel(c_2), .in(clk), .out_0(demultiplexer_1_out_0), .out_1(demultiplexer_1_out_1),
    .out_2(demultiplexer_1_out_2), .out_3(demultiplexer_1_out_3), .out_4(demultiplexer_1_out_4),
    .out_5(demultiplexer_1_out_5), .out_6(demultiplexer_1_out_6), .out_7(demultiplexer_1_out_7),
    .out_8(demultiplexer_1_out_8), .out_9(demultiplexer_1_out_9), .out_10(demultiplexer_1_out_10),
    .out_11(demultiplexer_1_out_11), .out_12(demultiplexer_1_out_12), .out_13(demultiplexer_1_out_13),
    .out_14(demultiplexer_1_out_14), .out_15(demultiplexer_1_out_15));
  Register #(.Bits(32)) register_1 (.D({32{1'b0}}), .C(demultiplexer_1_out_0), .en(escR), .Q(R0));
  Register #(.Bits(32)) register_2 (.D(C), .C(demultiplexer_1_out_15), .en(escR), .Q(R8));
  Register #(.Bits(32)) register_3 (.D(C), .C(demultiplexer_1_out_1), .en(escR), .Q(R1));
  Register #(.Bits(32)) register_4 (.D(C), .C(demultiplexer_1_out_14), .en(escR), .Q(R9));
  Register #(.Bits(32)) register_5 (.D(C), .C(demultiplexer_1_out_2), .en(escR), .Q(R2));
  Register #(.Bits(32)) register_6 (.D(C), .C(demultiplexer_1_out_13), .en(escR), .Q(R10));
  Multiplexer #(.Selector_Bits(4), .Bits(32)) multiplexer_1 (
    .sel(a_2), .in_0(R0), .in_1(R1), .in_2(R2), .in_3(R3), .in_4(R4), .in_5(R5), .in_6(R6), .in_7(R7),
    .in_8(R8), .in_9(R9), .in_10(R10), .in_11(R11), .in_12(R12), .in_13(R13), .in_14(R14), .in_15(R15),
    .out(A));
  Register #(.Bits(32)) register_7 (.D(C), .C(demultiplexer_1_out_3), .en(escR), .Q(R3));
  Register #(.Bits(32)) register_8 (.D(C), .C(demultiplexer_1_out_12), .en(escR), .Q(R11));
  Register #(.Bits(32)) register_9 (.D(C), .C(demultiplexer_1_out_4), .en(escR), .Q(R4));
  Register #(.Bits(32)) register_10 (.D(C), .C(demultiplexer_1_out_11), .en(escR), .Q(R12));
  Register #(.Bits(32)) register_11 (.D(C), .C(demultiplexer_1_out_5), .en(escR), .Q(R5));
  Register #(.Bits(32)) register_12 (.D(C), .C(demultiplexer_1_out_10), .en(escR), .Q(R13));
  Multiplexer #(.Selector_Bits(4), .Bits(32)) multiplexer_2 (
    .sel(b_2), .in_0(R0), .in_1(R1), .in_2(R2), .in_3(R3), .in_4(R4), .in_5(R5), .in_6(R6), .in_7(R7),
    .in_8(R8), .in_9(R9), .in_10(R10), .in_11(R11), .in_12(R12), .in_13(R13), .in_14(R14), .in_15(R15),
    .out(B));
  Register #(.Bits(32)) register_13 (.D(C), .C(demultiplexer_1_out_6), .en(escR), .Q(R6));
  Register #(.Bits(32)) register_14 (.D(C), .C(demultiplexer_1_out_9), .en(escR), .Q(R14));
  Register #(.Bits(32)) register_15 (.D(C), .C(demultiplexer_1_out_7), .en(escR), .Q(R7));
  Register #(.Bits(32)) register_16 (.D(C), .C(demultiplexer_1_out_8), .en(escR), .Q(R15));

  // Other names for the same wires on the sheet: en = escR
endmodule
