// Digital circuit micoXII.dig as structural Verilog
module micoXII (
  input  clk
);

  wire comparator_1_eq, escM, escR, selB, show;
  wire [0:0] rom_2_d;
  wire [1:0] proxIP, selC;
  wire [2:0] fun;
  wire [3:0] _0_3, _4_7, _8_11, _12_15, _16_19, _20_23, _24_27, _28_31, opcode;
  wire [15:0] addIP, \const , IP, multiplexer_1_out, multiplexer_2_out;
  wire [27:16] rom_1_d;
  wire [31:0] B, bitextender_1_out, bitextender_2_out, bitextender_3_out, bregs_1_a, multiplexer_3_out,
       multiplexer_4_out, ramdualport_1_d, ula_1_c;

  Comparator #(.Bits(32)) comparator_1 (
    .a({_28_31, _24_27, _20_23, _16_19, _12_15, _8_11, _4_7, _0_3}), .b(B), .eq(comparator_1_eq));  // open: gt, lt
  Add #(.Bits(16)) add_1 (.a(IP), .b(16'h1), .c_i(1'b0), .s(addIP));  // open: c_o
  Register #(.Bits(16)) u_IP (.D(multiplexer_2_out), .C(clk), .en(1'b1), .Q(IP));
  Multiplexer #(.Bits(16)) multiplexer_1 (.sel(comparator_1_eq), .in_0(addIP), .in_1(\const ), .out(multiplexer_1_out));
  Multiplexer #(.Selector_Bits(2), .Bits(16)) multiplexer_2 (
    .sel(proxIP), .in_0(addIP), .in_1(\const ), .in_2(multiplexer_1_out), .in_3({_12_15, _8_11, _4_7, _0_3}),
    .out(multiplexer_2_out));
  ROM #(.AddrBits(16), .Bits(32)) rom_1 (.A(IP), .sel(clk), .D({opcode, rom_1_d, \const }));
  bRegs bregs_1 (
    .C(multiplexer_4_out), .clk(clk), .a_2(rom_1_d[27:24]), .b_2(rom_1_d[23:20]), .c_2(rom_1_d[19:16]),
    .escR(escR), .A(bregs_1_a), .B(B));
  BitExtender #(.inputBits(16), .outputBits(32)) bitextender_1 (.in(\const ), .out(bitextender_1_out));
  Multiplexer #(.Bits(32)) multiplexer_3 (.sel(selB), .in_0(B), .in_1(bitextender_1_out), .out(multiplexer_3_out));
  ROM #(.AddrBits(4), .Bits(12)) rom_2 (
    .A(opcode), .sel(clk), .D({proxIP, escR, selB, fun, selC, escM, show, rom_2_d[0]}));
  Stop stop_1 (.stop(rom_2_d[0]));
  Seven_Seg_Hex seven_seg_hex_1 (.d(_28_31), .dp(1'b1));
  Demultiplexer #(.Bits(32)) demultiplexer_1 (
    .sel(show), .in(bregs_1_a), .out_0({_28_31, _24_27, _20_23, _16_19, _12_15, _8_11, _4_7, _0_3}),
    .out_1({_28_31, _24_27, _20_23, _16_19, _12_15, _8_11, _4_7, _0_3}));
  Seven_Seg_Hex seven_seg_hex_2 (.d(_24_27), .dp(1'b1));
  Seven_Seg_Hex seven_seg_hex_3 (.d(_20_23), .dp(1'b1));
  ULA ula_1 (.A(bregs_1_a), .B(multiplexer_3_out), .fun(fun), .C(ula_1_c));
  Seven_Seg_Hex seven_seg_hex_4 (.d(_16_19), .dp(1'b1));
  Seven_Seg_Hex seven_seg_hex_5 (.d(_12_15), .dp(1'b1));
  Multiplexer #(.Selector_Bits(2), .Bits(32)) multiplexer_4 (
    .sel(selC), .in_0(ula_1_c), .in_1(ramdualport_1_d), .in_2(bitextender_3_out), .in_3(bitextender_2_out),
    .out(multiplexer_4_out));
  Seven_Seg_Hex seven_seg_hex_6 (.d(_8_11), .dp(1'b1));
  Seven_Seg_Hex seven_seg_hex_7 (.d(_4_7), .dp(1'b1));
  Seven_Seg_Hex seven_seg_hex_8 (.d(_0_3), .dp(1'b1));
  BitExtender #(.inputBits(16), .outputBits(32)) bitextender_2 (.in(addIP), .out(bitextender_2_out));
  BitExtender #(.inputBits(16), .outputBits(32)) bitextender_3 (.in(addIP), .out(bitextender_3_out));
  RAMDualPort #(.AddrBits(16), .isProgramMemory("true"), .Bits(32)) ramdualport_1 (
    .A(ula_1_c[15:0]), .Din(B), .str(escM), .C(clk), .ld(clk), .D(ramdualport_1_d));

  // Other names for the same wires on the sheet: A[31:0] = {_28_31, _24_27, _20_23, _16_19, _12_15, _8_11, _4_7, _0_3}

  // Notes on the sheet:
  //   beq
  //   Memória de Instruções
  //   contents of rom_1 (hex, n*v repeats v):
  //   80010004,0,80020007,0,61230000,0,e0300030,0,21210000,0,c0000038
  //   ,0,11210000,0,71010000,0,b1000000,0,31240000,0,42460000,0,a2600002
  //   ,0,92050002,0,56550000,0,80070088,0,c0070038,0,6360000,0,b6000000
  //   ,0,f0000000
  //   display
  //   contents of rom_2 (hex, n*v repeats v):
  //   100,110,120,130,140,150,160,170,300,308,104,2,a10,c00,400,1
  //   Memória de Controle
  //   Memória de Dados
  //   clock
endmodule
