// Digital circuit ALU.dig as structural Verilog
module ALU (
  input  [31:0] A,
  input  [31:0] B,
  input  [2:0] ALUc,
  output Z,
  output [31:0] O
);

  wire add_1_c_o, comparator_1_eq, comparator_1_gt, comparator_1_lt, sub_1_c_o;
  wire [31:0] \and , \nor , \or , sll, slt, srl, sub, sum;

  assign \and  = A & B;  // And and_1, 32 bits wide
  assign \or  = A | B;  // Or or_1, 32 bits wide
  assign \nor  = ~(A | B);  // NOr nor_1, 32 bits wide
  Add #(.Bits(32)) add_1 (.a(A), .b(B), .c_i(1'b0), .s(sum), .c_o(add_1_c_o));
  Sub #(.Bits(32)) sub_1 (.a(A), .b(B), .c_i(1'b0), .s(sub), .c_o(sub_1_c_o));
  // Probe on add_1_c_o
  // Probe on sub_1_c_o
  Comparator #(.Bits(32)) comparator_1 (.a(A), .b(B), .gt(comparator_1_gt), .eq(comparator_1_eq), .lt(comparator_1_lt));
  BarrelShifter #(.Bits(32)) barrelshifter_1 (.in(A), .shift({1'b0, B[10:6]}), .out(sll));
  BarrelShifter #(.Bits(32), .direction("right")) barrelshifter_2 (.in(A), .shift({1'b0, B[10:6]}), .out(srl));
  BitExtender #(.inputBits(1), .outputBits(32)) bitextender_1 (.in(comparator_1_lt), .out(slt));
  // Probe on comparator_1_gt
  // Probe on comparator_1_eq
  Multiplexer #(.Selector_Bits(3), .Bits(32)) multiplexer_1 (
    .sel(ALUc), .in_0(\and ), .in_1(\or ), .in_2(\nor ), .in_3(sum), .in_4(sub), .in_5(slt), .in_6(sll),
    .in_7(srl), .out(O));
  nor nor_2 (Z, O[31], O[0], O[1], O[2], O[3], O[4], O[5], O[6], O[7], O[8], O[9], O[10], O[11], O[12], O[13], O[14], O[15], O[16], O[17], O[18], O[19], O[20], O[21], O[22], O[23], O[24], O[25], O[26], O[27], O[28], O[29], O[30]);

  // Notes on the sheet:
  //   Operations
  //   Out
endmodule
