// Digital circuit MIPS.dig as structural Verilog
module MIPS (
  input  clk
);

  wire add_1_c_o, alu_1_z, ALUSrc, and_1_out, MemRead, MemWrite, multiplexer_5_out, nor_1_out, not_1_out,
       not_2_out, RegWrite;
  wire [1:0] Branch, Jump, MemtoReg, RegDst;
  wire [2:0] multiplexer_3_out, rom_3_d, rom_4_d;
  wire [3:0] ALUOp;
  wire [4:0] multiplexer_1_out, RD, RS, RT;
  wire [27:0] Shift_Left_2_out;
  wire [31:0] add_1_s, add_3_s, alu_1_o, bitextender_1_out, Jal, Lui, multiplexer_2_out, multiplexer_4_out,
       multiplexer_7_out, PC, PC_q, ramdualport_1_d, regs_1_rdt1, regs_1_rdt2, rom_1_d, Shift_Left_3_out;

  Register #(.Bits(32), .isProgramCounter("true")) u_PC (.D(PC), .C(clk), .en(1'b1), .Q(PC_q));
  // Probe on PC_q
  Add #(.Bits(32)) add_1 (.a(PC_q), .b(32'h4), .c_i(1'b0), .s(add_1_s), .c_o(add_1_c_o));
  ROM #(.AddrBits(24), .Bits(32)) rom_1 (.A(PC_q[23:0]), .sel(1'b1), .D({rom_1_d[31:26], RS, RT, RD, rom_1_d[10:0]}));
  // Probe on add_1_c_o
  BarrelShifter #(.Bits(32)) Shift_Left (.in({{16{1'b0}}, RD, rom_1_d[10:0]}), .shift(6'b010000), .out(Lui));
  BarrelShifter #(.Bits(28)) Shift_Left_2 (
    .in({2'b00, RS, RT, RD, rom_1_d[10:0]}), .shift(5'b00010), .out(Shift_Left_2_out));
  ROM #(.AddrBits(6), .Bits(16)) rom_2 (
    .A(rom_1_d[31:26]), .sel(1'b1),
    .D({RegDst, Jump, Branch, MemtoReg, MemRead, MemWrite, ALUOp, ALUSrc, RegWrite}));
  Multiplexer #(.Selector_Bits(2), .Bits(5)) multiplexer_1 (
    .sel(RegDst), .in_0(RT), .in_1(RD), .in_2({5{1'b1}}), .in_3({5{1'b0}}), .out(multiplexer_1_out));
  RegS regs_1 (
    .clk(clk), .RR1(RS), .RR2(RT), .WR(multiplexer_1_out), .WD(multiplexer_7_out), .RW(RegWrite),
    .rDT1(regs_1_rdt1), .rDT2(regs_1_rdt2));
  BitExtender #(.inputBits(16), .outputBits(32)) bitextender_1 (.in({RD, rom_1_d[10:0]}), .out(bitextender_1_out));
  // Probe on ALUOp
  ROM #(.AddrBits(6), .Bits(3)) rom_3 (.A(rom_1_d[5:0]), .sel(ALUOp[3]), .D(rom_3_d));
  Multiplexer #(.Bits(32)) multiplexer_2 (
    .sel(ALUSrc), .in_0(regs_1_rdt2), .in_1(bitextender_1_out), .out(multiplexer_2_out));
  not not_1 (not_1_out, ALUOp[3]);
  Multiplexer #(.Bits(3)) multiplexer_3 (.sel(not_1_out), .in_0(rom_3_d), .in_1(rom_4_d), .out(multiplexer_3_out));
  BarrelShifter #(.Bits(32)) Shift_Left_3 (.in(bitextender_1_out), .shift(6'b000010), .out(Shift_Left_3_out));
  Add #(.Bits(32)) add_2 (.a(add_1_s), .b(32'h4), .c_i(1'b0), .s(Jal));  // open: c_o
  ALU alu_1 (.A(regs_1_rdt1), .B(multiplexer_2_out), .ALUc(multiplexer_3_out), .Z(alu_1_z), .O(alu_1_o));
  ROM #(.AddrBits(3), .Bits(3)) rom_4 (.A(ALUOp[2:0]), .sel(not_2_out), .D(rom_4_d));
  not not_2 (not_2_out, ALUOp[3]);
  Add #(.Bits(32)) add_3 (.a(Shift_Left_3_out), .b(add_1_s), .c_i(1'b0), .s(add_3_s));  // open: c_o
  and and_1 (and_1_out, alu_1_z, 1'b1);
  Multiplexer #(.Bits(32)) multiplexer_4 (
    .sel(multiplexer_5_out), .in_0(add_1_s), .in_1(add_3_s), .out(multiplexer_4_out));
  Multiplexer #(.Selector_Bits(2)) multiplexer_5 (
    .sel(Branch), .in_0(1'b0), .in_1(and_1_out), .in_2(nor_1_out), .in_3(1'b0), .out(multiplexer_5_out));
  nor nor_1 (nor_1_out, alu_1_z, 1'b0);
  RAMDualPort #(.AddrBits(24), .Bits(32)) ramdualport_1 (
    .A(alu_1_o[23:0]), .Din(regs_1_rdt2), .str(MemWrite), .C(clk), .ld(MemRead), .D(ramdualport_1_d));
  Multiplexer #(.Selector_Bits(2), .Bits(32)) multiplexer_6 (
    .sel(Jump), .in_0(multiplexer_4_out), .in_1({add_1_s[31:28], Shift_Left_2_out}), .in_2({32{1'b0}}),
    .in_3(regs_1_rdt1), .out(PC));
  Multiplexer #(.Selector_Bits(2), .Bits(32)) multiplexer_7 (
    .sel(MemtoReg), .in_0(alu_1_o), .in_1(ramdualport_1_d), .in_2(Lui), .in_3(Jal), .out(multiplexer_7_out));

  // Notes on the sheet:
  //   PC + 4
  //   Instruction Memory
  //   contents of rom_1 (hex, n*v repeats v):
  //   1801000c,0,0,0,18020010,0,0,0,18030004,0,0,0,40000008,0,0,0,14000003
  //   ,0,0,0,1c432004,0,0,0,38810002,0,0,0,14000003,0,0,0,48400000,0,0,0
  //   ,14000003,0,0,0,14632803,0,0,0,14a12803,0,0,0,2466000a,0,0,0,3cc00002
  //   ,0,0,0,14000003,0,0,0,1cc23004,0,0,0,4470000,0,0,0,e63800,0,0,0
  //   ,34270008,0,0,0,30080014,0,0,0,8e04001,0,0,0,d090000,0,0,0,11224802
  //   ,0,0,0,28035106,0,0,0,2c0158c7,0,0,0,216a6005,0,0,0,4c010002,0,0,0,44000001
  //   lui
  //   Instruction [25-0]
  //   PC+4 [31-28]
  //   Control
  //   Registers
  //   contents of rom_2 (hex, n*v repeats v):
  //   4021,3,4021,7,4021,4021,f,4021,4021,17,4021,4021,18f,4e,410,810
  //   ,1000,9301,3000,201
  //   ALU Control
  //   Jump Address [31-0]
  //   Tipo R
  //   contents of rom_3 (hex, n*v repeats v):
  //   0,1,2,3,4,5,6,7
  //   jal
  //   ALU
  //   beq/bne
  //   contents of rom_4 (hex, n*v repeats v):
  //   0,1,2,3,4,5,6,7
  //   Tipo i
  //   zero
  //   clock
  //   jump/jump register
endmodule
