// Digital circuit RegS.dig as structural Verilog
module RegS (
  input  clk,
  input  [4:0] RR1,
  input  [4:0] RR2,
  input  [4:0] WR,
  input  [31:0] WD,
  input  RW,
  output [31:0] rDT1,
  output [31:0] rDT2
);

  wire R0, R1, R2, R3, R4, R5, R6, R7, R8, R9, R10, R11, R12, R13, R14, R15, R16, R17, R18, R19, R20, R21,
       R22, R23, R24, R25, R26, R27, R28, R29, R30, R31;
  wire [31:0] S0, S1, S2, S3, S4, S5, S6, S7, S8, S9, S10, S11, S12, S13, S14, S15, S16, S17, S18, S19, S20,
       S21, S22, S23, S24, S25, S26, S27, S28, S29, S30, S31;

  Demultiplexer #(.Selector_Bits(5)) demultiplexer_1 (
    .sel(WR), .in(clk), .out_0(R0), .out_1(R1), .out_2(R2), .out_3(R3), .out_4(R4), .out_5(R5), .out_6(R6),
    .out_7(R7), .out_8(R8), .out_9(R9), .out_10(R10), .out_11(R11), .out_12(R12), .out_13(R13), .out_14(R14),
    .out_15(R15), .out_16(R16), .out_17(R17), .out_18(R18), .out_19(R19), .out_20(R20), .out_21(R21),
    .out_22(R22), .out_23(R23), .out_24(R24), .out_25(R25), .out_26(R26), .out_27(R27), .out_28(R28),
    .out_29(R29), .out_30(R30), .out_31(R31));
  Register #(.Bits(32)) u_R0 (.D({32{1'b0}}), .C(R0), .en(RW), .Q(S0));
  Register #(.Bits(32)) u_R8 (.D(WD), .C(R8), .en(RW), .Q(S8));
  Register #(.Bits(32)) u_R16 (.D(WD), .C(R16), .en(RW), .Q(S16));
  Register #(.Bits(32)) u_R24 (.D(WD), .C(R24), .en(RW), .Q(S24));
  Register #(.Bits(32)) u_R1 (.D(WD), .C(R1), .en(RW), .Q(S1));
  Register #(.Bits(32)) u_R9 (.D(WD), .C(R9), .en(RW), .Q(S9));
  Register #(.Bits(32)) u_R17 (.D(WD), .C(R17), .en(RW), .Q(S17));
  Register #(.Bits(32)) u_R25 (.D(WD), .C(R25), .en(RW), .Q(S25));
  Register #(.Bits(32)) u_R2 (.D(WD), .C(R2), .en(RW), .Q(S2));
  Register #(.Bits(32)) u_R10 (.D(WD), .C(R10), .en(RW), .Q(S10));
  Register #(.Bits(32)) u_R18 (.D(WD), .C(R18), .en(RW), .Q(S18));
  Register #(.Bits(32)) u_R26 (.D(WD), .C(R26), .en(RW), .Q(S26));
  Register #(.Bits(32)) u_R3 (.D(WD), .C(R3), .en(RW), .Q(S3));
  Register #(.Bits(32)) u_R11 (.D(WD), .C(R11), .en(RW), .Q(S11));
  Register #(.Bits(32)) u_R19 (.D(WD), .C(R19), .en(RW), .Q(S19));
  Register #(.Bits(32)) u_R27 (.D(WD), .C(R27), .en(RW), .Q(S27));
  Multiplexer #(.Bits(32), .Selector_Bits(5)) multiplexer_1 (
    .sel(RR1), .in_0(S0), .in_1(S1), .in_2(S2), .in_3(S3), .in_4(S4), .in_5(S5), .in_6(S6), .in_7(S7),
    .in_8(S8), .in_9(S9), .in_10(S10), .in_11(S11), .in_12(S12), .in_13(S13), .in_14(S14), .in_15(S15),
    .in_16(S16), .in_17(S17), .in_18(S18), .in_19(S19), .in_20(S20), .in_21(S21), .in_22(S22), .in_23(S23),
    .in_24(S24), .in_25(S25), .in_26(S26), .in_27(S27), .in_28(S28), .in_29(S28), .in_30(S30), .in_31(S31),
    .out(rDT1));
  Register #(.Bits(32)) u_R4 (.D(WD), .C(R4), .en(RW), .Q(S4));
  Register #(.Bits(32)) u_R12 (.D(WD), .C(R12), .en(RW), .Q(S12));
  Register #(.Bits(32)) u_R20 (.D(WD), .C(R20), .en(RW), .Q(S20));
  Register #(.Bits(32)) u_R28 (.D(WD), .C(R28), .en(RW), .Q(S28));
  Register #(.Bits(32)) u_R5 (.D(WD), .C(R5), .en(RW), .Q(S5));
  Register #(.Bits(32)) u_R13 (.D(WD), .C(R13), .en(RW), .Q(S13));
  Register #(.Bits(32)) u_R21 (.D(WD), .C(R21), .en(RW), .Q(S21));
  Register #(.Bits(32)) u_R29 (.D(WD), .C(R29), .en(RW), .Q(S29));
  Register #(.Bits(32)) u_R6 (.D(WD), .C(R6), .en(RW), .Q(S6));
  Register #(.Bits(32)) u_R14 (.D(WD), .C(R14), .en(RW), .Q(S14));
  Register #(.Bits(32)) u_R22 (.D(WD), .C(R22), .en(RW), .Q(S22));
  Register #(.Bits(32)) u_R30 (.D(WD), .C(R30), .en(RW), .Q(S30));
  Multiplexer #(.Selector_Bits(5), .Bits(32)) multiplexer_2 (
    .sel(RR2), .in_0(S0), .in_1(S1), .in_2(S2), .in_3(S3), .in_4(S4), .in_5(S5), .in_6(S6), .in_7(S7),
    .in_8(S8), .in_9(S9), .in_10(S10), .in_11(S11), .in_12(S12), .in_13(S13), .in_14(S14), .in_15(S15),
    .in_16(S16), .in_17(S17), .in_18(S18), .in_19(S19), .in_20(S20), .in_21(S21), .in_22(S22), .in_23(S23),
    .in_24(S24), .in_25(S25), .in_26(S26), .in_27(S27), .in_28(S28), .in_29(S28), .in_30(S30), .in_31(S31),
    .out(rDT2));
  Register #(.Bits(32)) u_R7 (.D(WD), .C(R7), .en(RW), .Q(S7));
  Register #(.Bits(32)) u_R15 (.D(WD), .C(R15), .en(RW), .Q(S15));
  Register #(.Bits(32)) u_R23 (.D(WD), .C(R23), .en(RW), .Q(S23));
  Register #(.Bits(32)) u_R31 (.D(WD), .C(R31), .en(RW), .Q(S31));

  // Notes on the sheet:
  //   Write Data
  //   WriteReg
  //   Write
  //   ReadReg 1
  //   ReadData 1
  //   ReadReg 2
  //   ReadData 2
endmodule
